# Fritzing sketch one-button (saved by Fritzing 0.8.7b)
breadboards: 1

parts:
  Part1 = Arduino Uno (Rev3)
  J1 = Basic Servo
  S1 = Pushbutton [package="[THT]"]

nets:
  N1: Part1.D9_PWM, J1.pulse
  5V: Part1.5V, J1.vcc
  GND: Part1.GND, J1.gnd
  N2: S1.Pin_1, S1.Pin_2
  N3: S1.Pin_3, S1.Pin_4
